# Fritzing sketch RC Sketch v1 (saved by Fritzing 0.9.1b)
breadboards: 1

parts:
  IC1 = H-Bridge [package=THT]
  M1 = DC Motor
  M2 = DC Motor
  Parte1 = Intel Galileo Gen2
  U1 = JOYSTICK-PSP1000 [package=joystick-psp1000]
  BAT1 = BC9VPC [package=bc9vpc]

nets:
  N1: IC1.1_2EN, IC1.3_4EN, IC1.VCC1, Parte1.5V, BAT1.V+
  N2: IC1.1A, Parte1.D11_PWM/MOSI
  N3: IC1.1Y, M1.pin_2
  GND1: IC1.GND1, IC1.GND2
  N4: IC1.2Y, M1.pin_1
  N5: IC1.2A, Parte1.D10_PWM/SS
  N6: IC1.3Y, M2.pin_2
  GND3: IC1.GND3, IC1.GND4
  N7: IC1.4Y, M2.pin_1
  N8: Parte1.A1, U1.Y
  N9: Parte1.A2, U1.X
